# Fritzing sketch arduino_universal_trigger (saved by Fritzing 0.9.0b)
breadboards: 1

parts:
  Part1 = Arduino Leonardo (Rev3b)
  S1 = Pushbutton [package="[THT]"]
  U1 = MOC3031-M [package=dil06]
  R2 = Resistor [tolerance=±5% resistance=470 package=THT]
  R3 = Resistor [tolerance=±5% resistance=10k package=THT]
  Q1 = NPN-Transistor [package="TO92 [THT]"]
  R4 = Resistor [tolerance=±5% resistance=10k package=THT]
  LED1 = LED - 5mm [color="Infrared (940nm)" package="5 mm [THT]"]
  R5 = Photocell (LDR) [package=THT]
  R6 = Resistor [tolerance=±5% resistance=220 package=THT]
  R7 = Resistor [tolerance=±5% resistance=220 package=THT]
  LED2 = LED - 5mm [color="Blue (470nm)" package="5 mm [THT]"]

nets:
  N1: Part1.D3_PWM/SCL, R4.Pin_1
  N2: Part1.D7, S1.Pin_1, S1.Pin_2, R3.Pin_0
  N3: Part1.5V, S1.Pin_3, S1.Pin_4, R5.pin_0
  N4: Part1.GND, R2.Pin_1, R3.Pin_1, Q1.E, LED1.anode, R6.Pin_1, R7.Pin_1
  N5: Part1.A0, R5.pin_1, R6.Pin_0
  N6: Part1.D9_PWM/A9, LED2.anode
  N7: Part1.D11_PWM, LED1.cathode
  N8: Part1.D13_PWM, U1.1
  N9: U1.2, R2.Pin_0
  N10: Q1.B, R4.Pin_0
  N11: R7.Pin_0, LED2.cathode

notes:
  To flash pin
  To camera connector pin
